// Logisim project CPU.circ as structural Verilog: 6 circuits, main circuit main
module main (
  input  reset,
  output [31:0] Instr,
  output RegWrite,
  output [4:0] RegAddr,
  output [31:0] RegData,
  output MemWrite,
  output [4:0] MemAddr,
  output [31:0] MemData
);

  wire ALUsrc, branch, branch_sel, clk, J_sel, MemtoReg, RegDst;
  wire [2:0] ALUcontrol;
  wire [31:0] alu_1_aluresult, and_1_out, bit_extender_1_out, bit_extender_2_out, bit_extender_3_out,
       branch_PC, grf_1_rd1, J_PC, multiplexer_2_out, multiplexer_3_out, multiplexer_4_out, PC_4, PC_q,
       ram_1_data, shifter_1_out, shifter_2_out;

  Clock clock_1 (.out(clk));
  Multiplexer #(.width(5)) multiplexer_1 (
    .in0(Instr[20:16]), .in1(Instr[15:11]), .out(RegAddr), .sel(RegDst));  // open: en
  Multiplexer #(.width(32)) multiplexer_2 (
    .in0(PC_4), .in1(branch_PC), .out(multiplexer_2_out), .sel(branch_sel));  // open: en
  Register #(.width(32)) PC (.D(multiplexer_3_out), .Q(PC_q), .clk(clk), .clr(reset));  // open: en
  Multiplexer #(.width(32)) multiplexer_3 (
    .in0(multiplexer_2_out), .in1(J_PC), .out(multiplexer_3_out), .sel(J_sel));  // open: en
  assign bit_extender_1_out = {{16{Instr[15]}}, Instr[15:0]};  // Bit_Extender bit_extender_1
  assign bit_extender_2_out = {{6{Instr[25]}}, Instr[25:0]};  // Bit_Extender bit_extender_2
  assign and_1_out = PC_4 & 32'hc0000000;  // AND_Gate and_1, 32 bits wide
  Shifter #(.width(32)) shifter_1 (.in(bit_extender_1_out), .\dist (5'b00010), .out(shifter_1_out));
  Shifter #(.width(32)) shifter_2 (.in(bit_extender_2_out), .\dist (5'b00010), .out(shifter_2_out));
  Controller controller_1 (
    .op(Instr[31:26]), .funct(Instr[5:0]), .RegWrite(RegWrite), .MemWrite(MemWrite), .branch(branch),
    .RegDst(RegDst), .ALUsrc(ALUsrc), .MemtoReg(MemtoReg), .ALUcontrol(ALUcontrol), .J(J_sel));
  GRF grf_1 (
    .A1(Instr[25:21]), .A2(Instr[20:16]), .A3(RegAddr), .WD(RegData), .RD1(grf_1_rd1), .RD2(MemData),
    .CLK(clk), .reset(reset), .we(RegWrite));
  Adder #(.width(32)) adder_1 (.a(PC_q), .b(32'h4), .out(PC_4));  // open: cin, cout
  Adder #(.width(32)) adder_2 (.a(shifter_1_out), .b(PC_4), .out(branch_PC));  // open: cin, cout
  assign J_PC = shifter_2_out | and_1_out;  // OR_Gate or_1, 32 bits wide
  assign bit_extender_3_out = {{16{Instr[15]}}, Instr[15:0]};  // Bit_Extender bit_extender_3
  ROM #(.addrWidth(5), .dataWidth(32)) rom_1 (.addr(PC_q[6:2]), .data(Instr));  // open: sel
  Multiplexer #(.width(32)) multiplexer_4 (
    .in0(MemData), .in1(bit_extender_3_out), .out(multiplexer_4_out), .sel(ALUsrc));  // open: en
  ALU alu_1 (
    .SrcA(grf_1_rd1), .SrcB(multiplexer_4_out),
    .ALUresult({alu_1_aluresult[31:7], MemAddr, alu_1_aluresult[1:0]}), .ALUcontrol(ALUcontrol));
  and and_2 (branch_sel, branch, alu_1_aluresult[0]);
  RAM #(.addrWidth(5), .dataWidth(32), .bus("separate")) ram_1 (
    .addr(MemAddr), .din(MemData), .data(ram_1_data), .str(MemWrite), .clk(clk), .clr(reset));  // open: sel, ld
  Multiplexer #(.width(32)) multiplexer_5 (
    .in0({alu_1_aluresult[31:7], MemAddr, alu_1_aluresult[1:0]}), .in1(ram_1_data), .out(RegData),
    .sel(MemtoReg));  // open: en

  // Other names for the same wires on the sheet: address[25:0] = Instr[25:0]; funct[5:0] = Instr[5:0];
  //   immediate[15:0] = Instr[15:0]; shamt[4:0] = Instr[10:6]; rd[4:0] = Instr[15:11]; rt[4:0] = Instr[20:16];
  //   rs[4:0] = Instr[25:21]; op[5:0] = Instr[31:26]

  // Notes on the sheet:
  //   offset
  //   J
  //   R类型目的寄存器是rd
  //   I类型目的寄存器是rt
  //   PC>>2
  //   只有sw把(rt)存进去
  //   指令存储器IM
  //   contents of rom_1 (hex, n*v repeats v):
  //   34080001 34090001 11090001 3c0a0000 1485021
  //   是branch指令 1 否则 0
  //   是J指令 1 否则 0
  //   srcA
  //   srcB
  //   是（rt）还是immediate
  //   选择要往寄存器存的是ALU结果  0 
  //   选择ALU的第二个源操作数（srcB）
  //   PC>>2
  //   ALUresult
  //   (rt)
  //   J
  //   还是从内存中取出来的数 1
  //   数据存储器DM
  //   选择要往寄存器存的是ALU结果  0 
  //   还是从内存中取出来的数 1
endmodule

module GRF (
  input  [4:0] A1,
  input  CLK,
  input  reset,
  input  we,
  input  [4:0] A2,
  input  [4:0] A3,
  input  [31:0] WD,
  output [31:0] RD1,
  output [31:0] RD2
);

  wire and_1_out, and_2_out, and_3_out, and_4_out, and_5_out, and_6_out, and_7_out, and_8_out, and_9_out,
       and_10_out, and_11_out, and_12_out, and_13_out, and_14_out, and_15_out, and_16_out, and_17_out,
       and_18_out, and_19_out, and_20_out, and_21_out, and_22_out, and_23_out, and_24_out, and_25_out,
       and_26_out, and_27_out, and_28_out, and_29_out, and_30_out, and_31_out, comparator_1_eq,
       comparator_2_eq, comparator_3_eq, comparator_4_eq, comparator_5_eq, comparator_6_eq, comparator_7_eq,
       comparator_8_eq, comparator_9_eq, comparator_10_eq, comparator_11_eq, comparator_12_eq,
       comparator_13_eq, comparator_14_eq, comparator_15_eq, comparator_16_eq, comparator_17_eq,
       comparator_18_eq, comparator_19_eq, comparator_20_eq, comparator_21_eq, comparator_22_eq,
       comparator_23_eq, comparator_24_eq, comparator_25_eq, comparator_26_eq, comparator_27_eq,
       comparator_28_eq, comparator_29_eq, comparator_30_eq, comparator_31_eq;
  wire [31:0] _0, _1, _2, _3, _4, _5, _6, _7, _8, _9, _10, _11, _12, _13, _14, _15, _16, _17, _18, _19, _20,
       _21, _22, _23, _24, _25, _26, _27, _28, _29, _30, _31, multiplexer_1_out, multiplexer_2_out,
       multiplexer_3_out, multiplexer_4_out, multiplexer_5_out, multiplexer_6_out, multiplexer_7_out,
       multiplexer_8_out, multiplexer_9_out, multiplexer_10_out, multiplexer_11_out, multiplexer_12_out,
       multiplexer_13_out, multiplexer_14_out, multiplexer_15_out, multiplexer_18_out, multiplexer_19_out,
       multiplexer_20_out, multiplexer_21_out, multiplexer_22_out, multiplexer_23_out, multiplexer_24_out,
       multiplexer_25_out, multiplexer_26_out, multiplexer_27_out, multiplexer_28_out, multiplexer_29_out,
       multiplexer_30_out, multiplexer_31_out, multiplexer_32_out, multiplexer_33_out;

  Comparator #(.width(5)) comparator_1 (.a(5'b00100), .b(A3), .eq(comparator_1_eq));  // open: gt, lt
  Comparator #(.width(5)) comparator_2 (.a(5'b01000), .b(A3), .eq(comparator_2_eq));  // open: gt, lt
  Comparator #(.width(5)) comparator_3 (.a(5'b01100), .b(A3), .eq(comparator_3_eq));  // open: gt, lt
  Comparator #(.width(5)) comparator_4 (.a(5'b10000), .b(A3), .eq(comparator_4_eq));  // open: gt, lt
  Comparator #(.width(5)) comparator_5 (.a(5'b10100), .b(A3), .eq(comparator_5_eq));  // open: gt, lt
  Comparator #(.width(5)) comparator_6 (.a(5'b11000), .b(A3), .eq(comparator_6_eq));  // open: gt, lt
  Comparator #(.width(5)) comparator_7 (.a(5'b11100), .b(A3), .eq(comparator_7_eq));  // open: gt, lt
  Multiplexer #(.width(32)) multiplexer_1 (.in0(_4), .in1(WD), .out(multiplexer_1_out), .sel(and_1_out));  // open: en
  and and_1 (and_1_out, comparator_1_eq, we);
  Multiplexer #(.width(32)) multiplexer_2 (.in0(_8), .in1(WD), .out(multiplexer_2_out), .sel(and_2_out));  // open: en
  and and_2 (and_2_out, comparator_2_eq, we);
  Multiplexer #(.width(32)) multiplexer_3 (.in0(_12), .in1(WD), .out(multiplexer_3_out), .sel(and_3_out));  // open: en
  and and_3 (and_3_out, comparator_3_eq, we);
  Multiplexer #(.width(32)) multiplexer_4 (.in0(_16), .in1(WD), .out(multiplexer_4_out), .sel(and_4_out));  // open: en
  and and_4 (and_4_out, comparator_4_eq, we);
  Multiplexer #(.width(32)) multiplexer_5 (.in0(_20), .in1(WD), .out(multiplexer_5_out), .sel(and_5_out));  // open: en
  and and_5 (and_5_out, comparator_5_eq, we);
  Multiplexer #(.width(32)) multiplexer_6 (.in0(_24), .in1(WD), .out(multiplexer_6_out), .sel(and_6_out));  // open: en
  and and_6 (and_6_out, comparator_6_eq, we);
  Multiplexer #(.width(32)) multiplexer_7 (.in0(_28), .in1(WD), .out(multiplexer_7_out), .sel(and_7_out));  // open: en
  and and_7 (and_7_out, comparator_7_eq, we);
  Register #(.width(32)) u__0 (.D({32{1'b0}}), .Q(_0), .clk(CLK), .clr(reset));  // open: en
  Register #(.width(32)) u__4 (.D(multiplexer_1_out), .Q(_4), .clk(CLK), .clr(reset));  // open: en
  Register #(.width(32)) u__8 (.D(multiplexer_2_out), .Q(_8), .clk(CLK), .clr(reset));  // open: en
  Register #(.width(32)) u__12 (.D(multiplexer_3_out), .Q(_12), .clk(CLK), .clr(reset));  // open: en
  Register #(.width(32)) u__16 (.D(multiplexer_4_out), .Q(_16), .clk(CLK), .clr(reset));  // open: en
  Register #(.width(32)) u__20 (.D(multiplexer_5_out), .Q(_20), .clk(CLK), .clr(reset));  // open: en
  Register #(.width(32)) u__24 (.D(multiplexer_6_out), .Q(_24), .clk(CLK), .clr(reset));  // open: en
  Register #(.width(32)) u__28 (.D(multiplexer_7_out), .Q(_28), .clk(CLK), .clr(reset));  // open: en
  Comparator #(.width(5)) comparator_8 (.a(5'b00001), .b(A3), .eq(comparator_8_eq));  // open: gt, lt
  Comparator #(.width(5)) comparator_9 (.a(5'b00101), .b(A3), .eq(comparator_9_eq));  // open: gt, lt
  Comparator #(.width(5)) comparator_10 (.a(5'b01001), .b(A3), .eq(comparator_10_eq));  // open: gt, lt
  Comparator #(.width(5)) comparator_11 (.a(5'b01101), .b(A3), .eq(comparator_11_eq));  // open: gt, lt
  Comparator #(.width(5)) comparator_12 (.a(5'b10001), .b(A3), .eq(comparator_12_eq));  // open: gt, lt
  Comparator #(.width(5)) comparator_13 (.a(5'b10101), .b(A3), .eq(comparator_13_eq));  // open: gt, lt
  Comparator #(.width(5)) comparator_14 (.a(5'b11001), .b(A3), .eq(comparator_14_eq));  // open: gt, lt
  Comparator #(.width(5)) comparator_15 (.a(5'b11101), .b(A3), .eq(comparator_15_eq));  // open: gt, lt
  Register #(.width(32)) u__1 (.D(multiplexer_8_out), .Q(_1), .clk(CLK), .clr(reset));  // open: en
  Multiplexer #(.width(32)) multiplexer_8 (.in0(_1), .in1(WD), .out(multiplexer_8_out), .sel(and_8_out));  // open: en
  and and_8 (and_8_out, comparator_8_eq, we);
  Register #(.width(32)) u__5 (.D(multiplexer_9_out), .Q(_5), .clk(CLK), .clr(reset));  // open: en
  Multiplexer #(.width(32)) multiplexer_9 (.in0(_5), .in1(WD), .out(multiplexer_9_out), .sel(and_9_out));  // open: en
  and and_9 (and_9_out, comparator_9_eq, we);
  Register #(.width(32)) u__9 (.D(multiplexer_10_out), .Q(_9), .clk(CLK), .clr(reset));  // open: en
  Multiplexer #(.width(32)) multiplexer_10 (
    .in0(_9), .in1(WD), .out(multiplexer_10_out), .sel(and_10_out));  // open: en
  and and_10 (and_10_out, comparator_10_eq, we);
  Register #(.width(32)) u__13 (.D(multiplexer_11_out), .Q(_13), .clk(CLK), .clr(reset));  // open: en
  Multiplexer #(.width(32)) multiplexer_11 (
    .in0(_13), .in1(WD), .out(multiplexer_11_out), .sel(and_11_out));  // open: en
  and and_11 (and_11_out, comparator_11_eq, we);
  Register #(.width(32)) u__17 (.D(multiplexer_12_out), .Q(_17), .clk(CLK), .clr(reset));  // open: en
  Multiplexer #(.width(32)) multiplexer_12 (
    .in0(_17), .in1(WD), .out(multiplexer_12_out), .sel(and_12_out));  // open: en
  and and_12 (and_12_out, comparator_12_eq, we);
  Multiplexer #(.width(32)) multiplexer_13 (
    .in0(_21), .in1(WD), .out(multiplexer_13_out), .sel(and_13_out));  // open: en
  Register #(.width(32)) u__21 (.D(multiplexer_13_out), .Q(_21), .clk(CLK), .clr(reset));  // open: en
  and and_13 (and_13_out, comparator_13_eq, we);
  Register #(.width(32)) u__25 (.D(multiplexer_14_out), .Q(_25), .clk(CLK), .clr(reset));  // open: en
  Multiplexer #(.width(32)) multiplexer_14 (
    .in0(_25), .in1(WD), .out(multiplexer_14_out), .sel(and_14_out));  // open: en
  and and_14 (and_14_out, comparator_14_eq, we);
  Multiplexer #(.width(32)) multiplexer_15 (
    .in0(_29), .in1(WD), .out(multiplexer_15_out), .sel(and_15_out));  // open: en
  Register #(.width(32)) u__29 (.D(multiplexer_15_out), .Q(_29), .clk(CLK), .clr(reset));  // open: en
  and and_15 (and_15_out, comparator_15_eq, we);
  Multiplexer #(.select(5), .width(32)) multiplexer_16 (
    .in0(_0), .in1(_1), .in2(_2), .in3(_3), .in4(_4), .in5(_5), .in6(_6), .in7(_7), .in8(_8), .in9(_9),
    .in10(_10), .in11(_11), .in12(_12), .in13(_13), .in14(_14), .in15(_15), .in16(_16), .in17(_17),
    .in18(_18), .in19(_19), .in20(_20), .in21(_21), .in22(_22), .in23(_23), .in24(_24), .in25(_25),
    .in26(_26), .in27(_27), .in28(_28), .in29(_29), .in30(_30), .in31(_31), .out(RD1), .sel(A1));  // open: en
  Multiplexer #(.select(5), .width(32)) multiplexer_17 (
    .in0(_0), .in1(_1), .in2(_2), .in3(_3), .in4(_4), .in5(_5), .in6(_6), .in7(_7), .in8(_8), .in9(_9),
    .in10(_10), .in11(_11), .in12(_12), .in13(_13), .in14(_14), .in15(_15), .in16(_16), .in17(_17),
    .in18(_18), .in19(_19), .in20(_20), .in21(_21), .in22(_22), .in23(_23), .in24(_24), .in25(_25),
    .in26(_26), .in27(_27), .in28(_28), .in29(_29), .in30(_30), .in31(_31), .out(RD2), .sel(A2));  // open: en
  Comparator #(.width(5)) comparator_16 (.a(5'b00010), .b(A3), .eq(comparator_16_eq));  // open: gt, lt
  Comparator #(.width(5)) comparator_17 (.a(5'b00110), .b(A3), .eq(comparator_17_eq));  // open: gt, lt
  Comparator #(.width(5)) comparator_18 (.a(5'b01010), .b(A3), .eq(comparator_18_eq));  // open: gt, lt
  Comparator #(.width(5)) comparator_19 (.a(5'b01110), .b(A3), .eq(comparator_19_eq));  // open: gt, lt
  Comparator #(.width(5)) comparator_20 (.a(5'b10010), .b(A3), .eq(comparator_20_eq));  // open: gt, lt
  Comparator #(.width(5)) comparator_21 (.a(5'b10110), .b(A3), .eq(comparator_21_eq));  // open: gt, lt
  Comparator #(.width(5)) comparator_22 (.a(5'b11010), .b(A3), .eq(comparator_22_eq));  // open: gt, lt
  Comparator #(.width(5)) comparator_23 (.a(5'b11110), .b(A3), .eq(comparator_23_eq));  // open: gt, lt
  and and_16 (and_16_out, comparator_16_eq, we);
  and and_17 (and_17_out, comparator_17_eq, we);
  and and_18 (and_18_out, comparator_18_eq, we);
  and and_19 (and_19_out, comparator_19_eq, we);
  and and_20 (and_20_out, comparator_20_eq, we);
  and and_21 (and_21_out, comparator_21_eq, we);
  and and_22 (and_22_out, comparator_22_eq, we);
  and and_23 (and_23_out, comparator_23_eq, we);
  Multiplexer #(.width(32)) multiplexer_18 (
    .in0(_2), .in1(WD), .out(multiplexer_18_out), .sel(and_16_out));  // open: en
  Register #(.width(32)) u__2 (.D(multiplexer_18_out), .Q(_2), .clk(CLK), .clr(reset));  // open: en
  Register #(.width(32)) u__6 (.D(multiplexer_19_out), .Q(_6), .clk(CLK), .clr(reset));  // open: en
  Multiplexer #(.width(32)) multiplexer_19 (
    .in0(_6), .in1(WD), .out(multiplexer_19_out), .sel(and_17_out));  // open: en
  Register #(.width(32)) u__10 (.D(multiplexer_20_out), .Q(_10), .clk(CLK), .clr(reset));  // open: en
  Multiplexer #(.width(32)) multiplexer_20 (
    .in0(_10), .in1(WD), .out(multiplexer_20_out), .sel(and_18_out));  // open: en
  Multiplexer #(.width(32)) multiplexer_21 (
    .in0(_14), .in1(WD), .out(multiplexer_21_out), .sel(and_19_out));  // open: en
  Register #(.width(32)) u__14 (.D(multiplexer_21_out), .Q(_14), .clk(CLK), .clr(reset));  // open: en
  Register #(.width(32)) u__18 (.D(multiplexer_22_out), .Q(_18), .clk(CLK), .clr(reset));  // open: en
  Multiplexer #(.width(32)) multiplexer_22 (
    .in0(_18), .in1(WD), .out(multiplexer_22_out), .sel(and_20_out));  // open: en
  Multiplexer #(.width(32)) multiplexer_23 (
    .in0(_22), .in1(WD), .out(multiplexer_23_out), .sel(and_21_out));  // open: en
  Register #(.width(32)) u__22 (.D(multiplexer_23_out), .Q(_22), .clk(CLK), .clr(reset));  // open: en
  Multiplexer #(.width(32)) multiplexer_24 (
    .in0(_26), .in1(WD), .out(multiplexer_24_out), .sel(and_22_out));  // open: en
  Register #(.width(32)) u__26 (.D(multiplexer_24_out), .Q(_26), .clk(CLK), .clr(reset));  // open: en
  Multiplexer #(.width(32)) multiplexer_25 (
    .in0(_30), .in1(WD), .out(multiplexer_25_out), .sel(and_23_out));  // open: en
  Register #(.width(32)) u__30 (.D(multiplexer_25_out), .Q(_30), .clk(CLK), .clr(reset));  // open: en
  Comparator #(.width(5)) comparator_24 (.a(5'b00011), .b(A3), .eq(comparator_24_eq));  // open: gt, lt
  Comparator #(.width(5)) comparator_25 (.a(5'b00111), .b(A3), .eq(comparator_25_eq));  // open: gt, lt
  Comparator #(.width(5)) comparator_26 (.a(5'b01011), .b(A3), .eq(comparator_26_eq));  // open: gt, lt
  Comparator #(.width(5)) comparator_27 (.a(5'b01111), .b(A3), .eq(comparator_27_eq));  // open: gt, lt
  Comparator #(.width(5)) comparator_28 (.a(5'b10011), .b(A3), .eq(comparator_28_eq));  // open: gt, lt
  Comparator #(.width(5)) comparator_29 (.a(5'b10111), .b(A3), .eq(comparator_29_eq));  // open: gt, lt
  Comparator #(.width(5)) comparator_30 (.a(5'b11011), .b(A3), .eq(comparator_30_eq));  // open: gt, lt
  Comparator #(.width(5)) comparator_31 (.a({5{1'b1}}), .b(A3), .eq(comparator_31_eq));  // open: gt, lt
  Multiplexer #(.width(32)) multiplexer_26 (
    .in0(_3), .in1(WD), .out(multiplexer_26_out), .sel(and_24_out));  // open: en
  and and_24 (and_24_out, comparator_24_eq, we);
  Multiplexer #(.width(32)) multiplexer_27 (
    .in0(_7), .in1(WD), .out(multiplexer_27_out), .sel(and_25_out));  // open: en
  and and_25 (and_25_out, comparator_25_eq, we);
  Multiplexer #(.width(32)) multiplexer_28 (
    .in0(_11), .in1(WD), .out(multiplexer_28_out), .sel(and_26_out));  // open: en
  and and_26 (and_26_out, comparator_26_eq, we);
  Multiplexer #(.width(32)) multiplexer_29 (
    .in0(_15), .in1(WD), .out(multiplexer_29_out), .sel(and_27_out));  // open: en
  and and_27 (and_27_out, comparator_27_eq, we);
  Multiplexer #(.width(32)) multiplexer_30 (
    .in0(_19), .in1(WD), .out(multiplexer_30_out), .sel(and_28_out));  // open: en
  and and_28 (and_28_out, comparator_28_eq, we);
  Multiplexer #(.width(32)) multiplexer_31 (
    .in0(_23), .in1(WD), .out(multiplexer_31_out), .sel(and_29_out));  // open: en
  and and_29 (and_29_out, comparator_29_eq, we);
  Multiplexer #(.width(32)) multiplexer_32 (
    .in0(_27), .in1(WD), .out(multiplexer_32_out), .sel(and_30_out));  // open: en
  and and_30 (and_30_out, comparator_30_eq, we);
  Multiplexer #(.width(32)) multiplexer_33 (
    .in0(_31), .in1(WD), .out(multiplexer_33_out), .sel(and_31_out));  // open: en
  and and_31 (and_31_out, comparator_31_eq, we);
  Register #(.width(32)) u__3 (.D(multiplexer_26_out), .Q(_3), .clk(CLK), .clr(reset));  // open: en
  Register #(.width(32)) u__7 (.D(multiplexer_27_out), .Q(_7), .clk(CLK), .clr(reset));  // open: en
  Register #(.width(32)) u__11 (.D(multiplexer_28_out), .Q(_11), .clk(CLK), .clr(reset));  // open: en
  Register #(.width(32)) u__15 (.D(multiplexer_29_out), .Q(_15), .clk(CLK), .clr(reset));  // open: en
  Register #(.width(32)) u__19 (.D(multiplexer_30_out), .Q(_19), .clk(CLK), .clr(reset));  // open: en
  Register #(.width(32)) u__23 (.D(multiplexer_31_out), .Q(_23), .clk(CLK), .clr(reset));  // open: en
  Register #(.width(32)) u__27 (.D(multiplexer_32_out), .Q(_27), .clk(CLK), .clr(reset));  // open: en
  Register #(.width(32)) u__31 (.D(multiplexer_33_out), .Q(_31), .clk(CLK), .clr(reset));  // open: en
endmodule

module Controller (
  input  [5:0] op,
  input  [5:0] funct,
  output MemtoReg,
  output MemWrite,
  output [2:0] ALUcontrol,
  output ALUsrc,
  output RegDst,
  output RegWrite,
  output branch,
  output J
);

  wire addu, beq, lui, lw, not_1_out, not_2_out, not_3_out, not_4_out, not_5_out, not_6_out, not_7_out,
       not_8_out, not_9_out, not_10_out, not_11_out, not_12_out, ori, R, subu, sw;

  not not_1 (not_1_out, op[5]);
  not not_2 (not_2_out, op[4]);
  not not_3 (not_3_out, op[2]);
  not not_4 (not_4_out, op[3]);
  not not_5 (not_5_out, op[1]);
  not not_6 (not_6_out, op[0]);
  and _001101 (ori, not_1_out, not_2_out, op[3], op[2], not_5_out, op[0]);
  and _100011 (lw, op[5], not_2_out, not_4_out, not_3_out, op[1], op[0]);
  and _101011 (sw, op[5], not_2_out, op[3], not_3_out, op[1], op[0]);
  and _000100 (beq, not_1_out, not_2_out, not_4_out, op[2], not_5_out, not_6_out);
  and _001111 (lui, not_1_out, not_2_out, op[3], op[2], op[1], op[0]);
  and _000010 (J, not_1_out, not_2_out, not_4_out, not_3_out, op[1], not_6_out);
  not not_7 (not_7_out, funct[5]);
  not not_8 (not_8_out, funct[4]);
  not not_9 (not_9_out, funct[3]);
  not not_10 (not_10_out, funct[2]);
  not not_11 (not_11_out, funct[1]);
  not not_12 (not_12_out, funct[0]);
  and and_1 (R, not_1_out, not_2_out, not_4_out, not_3_out, not_5_out, not_6_out);
  and _100001 (addu, funct[5], not_8_out, not_9_out, not_10_out, not_11_out, funct[0], R);
  and _100011_2 (subu, funct[5], not_8_out, not_9_out, not_10_out, funct[1], funct[0], R);
  buf or_1 (MemtoReg, lw);  // OR_Gate
  buf or_2 (MemWrite, sw);  // OR_Gate
  or or_3 (ALUsrc, ori, lw, sw, lui);
  or or_4 (RegDst, addu, subu);
  or or_5 (RegWrite, lw, addu, subu, ori, lui);
  buf or_6 (branch, beq);  // OR_Gate
  or or_7 (ALUcontrol[0], subu, lw, sw, lui);
  or or_8 (ALUcontrol[1], ori, lw, sw);
  or or_9 (ALUcontrol[2], beq, lui);

  // Other names for the same wires on the sheet: ALUconrtol0 = ALUcontrol[0]; ALUconrtol1 = ALUcontrol[1];
  //   ALUconrtol2 = ALUcontrol[2]

  // Notes on the sheet:
  //   addu
  //   ori
  //   subu
  //   lw
  //   sw
  //   beq
  //   lui
  //   是（rt）0还是immediate1
  //   不能用是否为R型指令来 选目的寄存器是否为rd jr指令是R型但不对寄存器写
  //   是branch指令 1 否则 0
  //   是J指令 1 否则 0
  //   选择要往寄存器存的是ALU结果  0 
  //   还是从内存中取出来的数 1
  //   选择ALU的第二个源操作数（srcB）
  //   选择要存的目的寄存器是rt 0 还是rd 1 
  //   3  2  1  0
  //   addu  0  0  0  0
  //   subu 0  0  0  1
  //   ori  0  0  1  0
  //   lw/sw  0  0  1  1
  //   beq  0  1  0  0
  //   lui  0  1  0  1
endmodule

module ALU (
  input  [2:0] ALUcontrol,
  input  [31:0] SrcA,
  input  [31:0] SrcB,
  output [31:0] ALUresult
);

  wire comparator_1_eq;
  wire [31:0] addu_result, and_1_out, beq_result, lui_result, lw_sw_result, ori_result, subu_result;

  Adder #(.width(32)) adder_1 (.a(SrcA), .b(SrcB), .out(addu_result));  // open: cin, cout
  Subtractor #(.width(32)) subtractor_1 (.a(SrcA), .b(SrcB), .out(subu_result));  // open: bin, bout
  assign and_1_out = SrcB & 32'hffff;  // AND_Gate and_1, 32 bits wide
  Adder #(.width(32)) adder_2 (.a(SrcA), .b(SrcB), .out(lw_sw_result));  // open: cin, cout
  assign beq_result = {{31{1'b0}}, comparator_1_eq};  // Bit_Extender bit_extender_1
  Comparator #(.width(32)) comparator_1 (.a(SrcA), .b(SrcB), .eq(comparator_1_eq));  // open: gt, lt
  Shifter #(.width(32)) shifter_1 (.in(SrcB), .\dist (5'b10000), .out(lui_result));
  assign ori_result = SrcA | and_1_out;  // OR_Gate or_1, 32 bits wide
  Multiplexer #(.select(3), .width(32)) multiplexer_1 (
    .in0(addu_result), .in1(subu_result), .in2(ori_result), .in3(lw_sw_result), .in4(beq_result),
    .in5(lui_result), .out(ALUresult), .sel(ALUcontrol));  // open: in6, in7, en

  // Notes on the sheet:
  //   base
  //   offset是字节数 不用再左移2位了
  //   或逻辑immediate要0扩展
  //   3  2  1  0
  //   addu  0  0  0  0
  //   subu 0  0  0  1
  //   ori  0  0  1  0
  //   lw/sw  0  0  1  1
  //   beq  0  1   0  0
  //   lui  0  1  0  1
endmodule

module cpu_sb (
  input  reset,
  output [31:0] Instr,
  output RegWrite,
  output [4:0] RegAddr,
  output [31:0] RegData,
  output MemWrite,
  output [4:0] MemAddr,
  output [31:0] MemData
);

  wire ALUsrc, branch, branch_sel, clk, J_sel, MemtoReg, RegDst, sb;
  wire [1:0] low2;
  wire [2:0] ALUcontrol;
  wire [31:0] and_1_out, and_3_out, and_4_out, and_5_out, and_6_out, bit_extender_1_out, bit_extender_2_out,
       bit_extender_3_out, branch_PC, byte0, byte1, byte2, byte3, grf_1_rd1, J_PC, Membyte, Membyte0,
       Membyte1, Membyte2, Membyte3, Memread, multiplexer_2_out, multiplexer_3_out, multiplexer_4_out,
       multiplexer_5_out, PC_4, PC_q, shifter_3_out, shifter_4_out;
  wire [31:7] alu_1_aluresult;

  Clock clock_1 (.out(clk));
  Multiplexer #(.width(5)) multiplexer_1 (
    .in0(Instr[20:16]), .in1(Instr[15:11]), .out(RegAddr), .sel(RegDst));  // open: en
  Multiplexer #(.width(32)) multiplexer_2 (
    .in0(PC_4), .in1(branch_PC), .out(multiplexer_2_out), .sel(branch_sel));  // open: en
  Shifter #(.width(32)) shifter_1 (.in(MemData), .\dist (5'b11000), .out(byte3));
  Register #(.width(32)) PC (.D(multiplexer_3_out), .Q(PC_q), .clk(clk), .clr(reset));  // open: en
  Multiplexer #(.width(32)) multiplexer_3 (
    .in0(multiplexer_2_out), .in1(J_PC), .out(multiplexer_3_out), .sel(J_sel));  // open: en
  assign bit_extender_1_out = {{16{Instr[15]}}, Instr[15:0]};  // Bit_Extender bit_extender_1
  assign bit_extender_2_out = {{6{Instr[25]}}, Instr[25:0]};  // Bit_Extender bit_extender_2
  assign and_1_out = PC_4 & 32'hc0000000;  // AND_Gate and_1, 32 bits wide
  Shifter #(.width(32), .shift("lr")) shifter_2 (.in(byte3), .\dist (5'b01000), .out(byte2));
  Shifter #(.width(32)) shifter_3 (.in(bit_extender_1_out), .\dist (5'b00010), .out(shifter_3_out));
  Shifter #(.width(32)) shifter_4 (.in(bit_extender_2_out), .\dist (5'b00010), .out(shifter_4_out));
  GRF grf_1 (
    .A1(Instr[25:21]), .A2(Instr[20:16]), .A3(RegAddr), .WD(RegData), .RD1(grf_1_rd1), .RD2(MemData),
    .CLK(clk), .reset(reset), .we(RegWrite));
  Shifter #(.width(32), .shift("lr")) shifter_5 (.in(byte2), .\dist (5'b01000), .out(byte1));
  Adder #(.width(32)) adder_1 (.a(PC_q), .b(32'h4), .out(PC_4));  // open: cin, cout
  Adder #(.width(32)) adder_2 (.a(shifter_3_out), .b(PC_4), .out(branch_PC));  // open: cin, cout
  assign J_PC = shifter_4_out | and_1_out;  // OR_Gate or_1, 32 bits wide
  Controller_sb controller_sb_1 (
    .op(Instr[31:26]), .funct(Instr[5:0]), .MemtoReg(MemtoReg), .MemWrite(MemWrite), .ALUcontrol(ALUcontrol),
    .ALUsrc(ALUsrc), .RegDst(RegDst), .RegWrite(RegWrite), .branch(branch), .J(J_sel), .sb(sb));
  assign bit_extender_3_out = {{16{Instr[15]}}, Instr[15:0]};  // Bit_Extender bit_extender_3
  Shifter #(.width(32), .shift("lr")) shifter_6 (.in(byte1), .\dist (5'b01000), .out(byte0));
  ROM #(.addrWidth(5), .dataWidth(32)) rom_1 (.addr(PC_q[6:2]), .data(Instr));  // open: sel
  Multiplexer #(.width(32)) multiplexer_4 (
    .in0(MemData), .in1(bit_extender_3_out), .out(multiplexer_4_out), .sel(ALUsrc));  // open: en
  ALU alu_1 (
    .SrcA(grf_1_rd1), .SrcB(multiplexer_4_out), .ALUresult({alu_1_aluresult, MemAddr, low2}),
    .ALUcontrol(ALUcontrol));
  and and_2 (branch_sel, branch, low2[0]);
  assign and_3_out = Memread & 32'hffffff00;  // AND_Gate and_3, 32 bits wide
  assign and_4_out = Memread & 32'hffff00ff;  // AND_Gate and_4, 32 bits wide
  assign and_5_out = Memread & 32'hff00ffff;  // AND_Gate and_5, 32 bits wide
  assign and_6_out = Memread & 32'hffffff;  // AND_Gate and_6, 32 bits wide
  Multiplexer #(.width(32)) multiplexer_5 (
    .in0(MemData), .in1(Membyte), .out(multiplexer_5_out), .sel(sb));  // open: en
  assign Membyte0 = and_3_out | byte0;  // OR_Gate or_2, 32 bits wide
  assign Membyte1 = and_4_out | byte1;  // OR_Gate or_3, 32 bits wide
  assign Membyte2 = and_5_out | byte2;  // OR_Gate or_4, 32 bits wide
  assign Membyte3 = and_6_out | byte3;  // OR_Gate or_5, 32 bits wide
  RAM #(.addrWidth(5), .dataWidth(32), .bus("separate")) ram_1 (
    .addr(MemAddr), .din(multiplexer_5_out), .data(Memread), .str(MemWrite), .clk(clk), .clr(reset));  // open: sel, ld
  Multiplexer #(.width(32)) multiplexer_6 (
    .in0({alu_1_aluresult, MemAddr, low2}), .in1(Memread), .out(RegData), .sel(MemtoReg));  // open: en
  Multiplexer #(.select(2), .width(32)) multiplexer_7 (
    .in0(Membyte0), .in1(Membyte1), .in2(Membyte2), .in3(Membyte3), .out(Membyte), .sel(low2));  // open: en

  // Other names for the same wires on the sheet: address[25:0] = Instr[25:0]; funct[5:0] = Instr[5:0];
  //   immediate[15:0] = Instr[15:0]; shamt[4:0] = Instr[10:6]; rd[4:0] = Instr[15:11]; rt[4:0] = Instr[20:16];
  //   rs[4:0] = Instr[25:21]; op[5:0] = Instr[31:26]

  // Notes on the sheet:
  //   offset
  //   J
  //   R类型目的寄存器是rd
  //   I类型目的寄存器是rt
  //   PC>>2
  //   只有sw把(rt)存进去
  //   指令存储器IM
  //   contents of rom_1 (hex, n*v repeats v):
  //   35080012 a0080000 35290034 a0090001 354a0056 a00a0002 356b0078 a00b0003
  //   是J指令 1 否则 0
  //   srcA
  //   srcB
  //   是（rt）还是immediate
  //   选择要往寄存器存的是ALU结果  0 
  //   是branch指令 1 否则 0
  //   选择ALU的第二个源操作数（srcB）
  //   (rt)
  //   ALUresult
  //   J
  //   还是从内存中取出来的数 1
  //   PC>>2
  //   数据存储器DM
  //   选择要往寄存器存的是ALU结果  0 
  //   还是从内存中取出来的数 1
endmodule

module Controller_sb (
  input  [5:0] op,
  input  [5:0] funct,
  output MemtoReg,
  output MemWrite,
  output [2:0] ALUcontrol,
  output ALUsrc,
  output RegDst,
  output RegWrite,
  output branch,
  output J,
  output sb
);

  wire addu, beq, lui, lw, not_1_out, not_2_out, not_3_out, not_4_out, not_5_out, not_6_out, not_7_out,
       not_8_out, not_9_out, not_10_out, not_11_out, not_12_out, ori, R, subu, sw;

  not not_1 (not_1_out, op[5]);
  not not_2 (not_2_out, op[4]);
  not not_3 (not_3_out, op[2]);
  not not_4 (not_4_out, op[3]);
  not not_5 (not_5_out, op[0]);
  not not_6 (not_6_out, op[1]);
  and _001101 (ori, not_1_out, not_2_out, op[3], op[2], not_6_out, op[0]);
  and _100011 (lw, op[5], not_2_out, not_4_out, not_3_out, op[1], op[0]);
  and _101011 (sw, op[5], not_2_out, op[3], not_3_out, op[1], op[0]);
  and _000100 (beq, not_1_out, not_2_out, not_4_out, op[2], not_6_out, not_5_out);
  and _001111 (lui, not_1_out, not_2_out, op[3], op[2], op[1], op[0]);
  and _000010 (J, not_1_out, not_2_out, not_4_out, not_3_out, op[1], not_5_out);
  and _000010_2 (sb, op[5], not_2_out, op[3], not_3_out, not_6_out, not_5_out);
  not not_7 (not_7_out, funct[5]);
  not not_8 (not_8_out, funct[4]);
  not not_9 (not_9_out, funct[3]);
  not not_10 (not_10_out, funct[2]);
  not not_11 (not_11_out, funct[1]);
  not not_12 (not_12_out, funct[0]);
  and and_1 (R, not_1_out, not_2_out, not_4_out, not_3_out, not_6_out, not_5_out);
  and _100001 (addu, funct[5], not_8_out, not_9_out, not_10_out, not_11_out, funct[0], R);
  and _100011_2 (subu, funct[5], not_8_out, not_9_out, not_10_out, funct[1], funct[0], R);
  buf or_1 (MemtoReg, lw);  // OR_Gate
  or or_2 (MemWrite, sw, sb);
  or or_3 (ALUsrc, ori, lw, sw, lui, sb);
  or or_4 (RegDst, addu, subu);
  or or_5 (RegWrite, lw, addu, subu, ori, lui);
  buf or_6 (branch, beq);  // OR_Gate
  or or_7 (ALUcontrol[0], subu, lw, sw, lui, sb);
  or or_8 (ALUcontrol[1], ori, lw, sw, sb);
  or or_9 (ALUcontrol[2], beq, lui);

  // Other names for the same wires on the sheet: ALUconrtol0 = ALUcontrol[0]; ALUconrtol1 = ALUcontrol[1];
  //   ALUconrtol2 = ALUcontrol[2]

  // Notes on the sheet:
  //   addu
  //   ori
  //   subu
  //   lw
  //   sw
  //   beq
  //   lui
  //   sb
  //   是（rt）0还是immediate1
  //   不能用是否为R型指令来 选目的寄存器是否为rd jr指令是R型但不对寄存器写
  //   是branch指令 1 否则 0
  //   是J指令 1 否则 0
  //   是J指令 1 否则 0
  //   选择要往寄存器存的是ALU结果  0 
  //   还是从内存中取出来的数 1
  //   选择ALU的第二个源操作数（srcB）
  //   选择要存的目的寄存器是rt 0 还是rd 1 
  //   3  2  1  0
  //   addu  0  0  0  0
  //   subu 0  0  0  1
  //   ori  0  0  1  0
  //   lw/sw/sb  0  0  1  1
  //   beq  0  1  0  0
  //   lui  0  1  0  1
endmodule
